// Logisim project logisim_reference.circ as structural Verilog: 25 circuits, main circuit main
module main (
  input  [15:0] BUS_1,
  input  man_bus_load
);

  wire comp_arator_1_cc_n, comp_arator_1_cc_z, control_unit_1_clck, control_unit_1_gpr_in,
       control_unit_1_gpr_out, control_unit_1_ir_in, control_unit_1_load_mm, control_unit_1_mar_in,
       control_unit_1_mdr_in, control_unit_1_mdr_out, control_unit_1_psw_in, control_unit_1_psw_out,
       control_unit_1_read_mm, control_unit_1_rom_8_out, control_unit_1_timer_in, control_unit_1_y_in,
       control_unit_1_y_offset_in, control_unit_1_y_out, control_unit_1_y_shift_left,
       control_unit_1_y_shift_right, control_unit_1_z_in, control_unit_1_z_out, ir_1_s, timer_1_timeout;
  wire [1:0] ir_1_shift;
  wire [2:0] control_unit_1_alu_control, control_unit_1_gpr_select, ir_1_rd_out_1, ir_1_rd_out_2, ir_1_rs1,
       ir_1_rs2, psw_1_cc_z;
  wire [3:0] ir_1_opcode_out;
  wire [15:0] alu_1_alu_out, controlled_buffer_1_out, mar_1_to_mm, mdr_new_1_to_mm, ra_m_1_mdr_from_mm,
       shift_1_to_alu, y_1_to_shifter;

  assign controlled_buffer_1_out = man_bus_load ? BUS_1 : 16'bz;  // Controlled_Buffer controlled_buffer_1
  MAR mar_1 (
    .BUS_in(controlled_buffer_1_out), .MAR_in(control_unit_1_mar_in), .Read_MM(control_unit_1_read_mm),
    .Load_MM(control_unit_1_load_mm), .To_MM(mar_1_to_mm));
  RA_M ra_m_1 (
    .MAR_To_MM(mar_1_to_mm), .Load_MM(control_unit_1_load_mm), .Read_MM(control_unit_1_read_mm),
    .MDR_To_MM(mdr_new_1_to_mm), .MDR_From_MM(ra_m_1_mdr_from_mm));
  MDR_new mdr_new_1 (
    .MDR_in(control_unit_1_mdr_in), .Read_MM(control_unit_1_read_mm), .BUS_in(controlled_buffer_1_out),
    .MDR_out(control_unit_1_mdr_out), .Load_MM(control_unit_1_load_mm), .From_MM(ra_m_1_mdr_from_mm),
    .BUS_out(controlled_buffer_1_out), .To_MM(mdr_new_1_to_mm));
  IR ir_1 (
    .BUS_in(controlled_buffer_1_out), .IR_in(control_unit_1_ir_in), .Rd_out_2(ir_1_rd_out_2), .Rs1(ir_1_rs1),
    .Rs2(ir_1_rs2), .Rd_out_1(ir_1_rd_out_1), .OPCODE_out(ir_1_opcode_out), .S(ir_1_s), .Shift(ir_1_shift));
  control_unit control_unit_1 (
    .IR_opcode(ir_1_opcode_out), .PSW_0_1_2(psw_1_cc_z), .IR_Rs2(ir_1_rs2), .TIMEOUT(timer_1_timeout),
    .ALU_control(control_unit_1_alu_control), .Clck(control_unit_1_clck), .GPR_in(control_unit_1_gpr_in),
    .GPR_out(control_unit_1_gpr_out), .GPR_select(control_unit_1_gpr_select), .IR_in(control_unit_1_ir_in),
    .Load_MM(control_unit_1_load_mm), .MAR_in(control_unit_1_mar_in), .MDR_in(control_unit_1_mdr_in),
    .MDR_out(control_unit_1_mdr_out), .PSW_in(control_unit_1_psw_in), .PSW_out(control_unit_1_psw_out),
    .Read_MM(control_unit_1_read_mm), .ROM_8_out(control_unit_1_rom_8_out),
    .Timer_In(control_unit_1_timer_in), .Y_in(control_unit_1_y_in), .Y_offset_in(control_unit_1_y_offset_in),
    .Y_out(control_unit_1_y_out), .Y_shift_left(control_unit_1_y_shift_left),
    .Y_shift_right(control_unit_1_y_shift_right), .Z_in(control_unit_1_z_in), .Z_out(control_unit_1_z_out));
  GPR_Full gpr_full_1 (
    .Rd_1(ir_1_rd_out_1), .Rd_2(ir_1_rd_out_2), .Rs_1(ir_1_rs1), .Rs_2(ir_1_rs2),
    .GPR_in(control_unit_1_gpr_in), .GPR_out(control_unit_1_gpr_out), .BUS_in(controlled_buffer_1_out),
    .GPR_sel(control_unit_1_gpr_select), .BUS_out(controlled_buffer_1_out));
  Y y_1 (
    .Y_in(control_unit_1_y_in), .Y_offset_in(control_unit_1_y_offset_in), .BUS_in(controlled_buffer_1_out),
    .Y_out(control_unit_1_y_out), .To_shifter(y_1_to_shifter), .Bus_output(controlled_buffer_1_out));
  Shift shift_1 (
    .Y_shift_right(control_unit_1_y_shift_right), .from_Y(y_1_to_shifter),
    .Y_shift_left(control_unit_1_y_shift_left), .shift_amount(ir_1_shift), .to_ALU(shift_1_to_alu));
  ALU alu_1 (
    .ALU_control(control_unit_1_alu_control), .bus_input(controlled_buffer_1_out),
    .Y_shifted_input(shift_1_to_alu), .ALU_out(alu_1_alu_out));
  Z z_1 (
    .Zin(control_unit_1_z_in), .ALU_input(alu_1_alu_out), .Zout(control_unit_1_z_out),
    .BUS_out(controlled_buffer_1_out));
  Comp_arator comp_arator_1 (.from_ALU(alu_1_alu_out), .CC_Z(comp_arator_1_cc_z), .CC_N(comp_arator_1_cc_n));
  PSW psw_1 (
    .IR_S(ir_1_s), .bus_input(controlled_buffer_1_out), .Z_in(control_unit_1_z_in),
    .PSW_out(control_unit_1_psw_out), .IR_opcode(ir_1_opcode_out), .PSW_in(control_unit_1_psw_in),
    .CC_Z_in(comp_arator_1_cc_z), .CC_N_in(comp_arator_1_cc_n), .bus_output(controlled_buffer_1_out),
    .CC_Z(psw_1_cc_z[0]), .CC_N(psw_1_cc_z[1]), .P(psw_1_cc_z[2]));
  timer timer_1 (
    .Timer_In(control_unit_1_timer_in), .Clock(control_unit_1_clck), .Bus_input(controlled_buffer_1_out),
    .TIMEOUT(timer_1_timeout));
  CONROM conrom_1 (.ROM_8_Out(control_unit_1_rom_8_out), .Bus_output(controlled_buffer_1_out));
endmodule

module logical_AND (
  input  [15:0] Bus_input,
  input  [15:0] Y_shifted_input,
  output [15:0] AND_output
);

  and and_1 (AND_output[0], Bus_input[0], Y_shifted_input[0]);
  and and_2 (AND_output[1], Bus_input[1], Y_shifted_input[1]);
  and and_3 (AND_output[2], Bus_input[2], Y_shifted_input[2]);
  and and_4 (AND_output[3], Bus_input[3], Y_shifted_input[3]);
  and and_5 (AND_output[4], Bus_input[4], Y_shifted_input[4]);
  and and_6 (AND_output[5], Bus_input[5], Y_shifted_input[5]);
  and and_7 (AND_output[6], Bus_input[6], Y_shifted_input[6]);
  and and_8 (AND_output[7], Bus_input[7], Y_shifted_input[7]);
  and and_9 (AND_output[8], Bus_input[8], Y_shifted_input[8]);
  and and_10 (AND_output[9], Bus_input[9], Y_shifted_input[9]);
  and and_11 (AND_output[10], Bus_input[10], Y_shifted_input[10]);
  and and_12 (AND_output[11], Bus_input[11], Y_shifted_input[11]);
  and and_13 (AND_output[12], Bus_input[12], Y_shifted_input[12]);
  and and_14 (AND_output[13], Bus_input[13], Y_shifted_input[13]);
  and and_15 (AND_output[14], Bus_input[14], Y_shifted_input[14]);
  and and_16 (AND_output[15], Bus_input[15], Y_shifted_input[15]);
endmodule

module logical_OR (
  input  [15:0] Bus_input,
  input  [15:0] Y_shifted_input,
  output [15:0] OR_output
);

  or or_1 (OR_output[0], Bus_input[0], Y_shifted_input[0]);
  or or_2 (OR_output[1], Bus_input[1], Y_shifted_input[1]);
  or or_3 (OR_output[2], Bus_input[2], Y_shifted_input[2]);
  or or_4 (OR_output[3], Bus_input[3], Y_shifted_input[3]);
  or or_5 (OR_output[4], Bus_input[4], Y_shifted_input[4]);
  or or_6 (OR_output[5], Bus_input[5], Y_shifted_input[5]);
  or or_7 (OR_output[6], Bus_input[6], Y_shifted_input[6]);
  or or_8 (OR_output[7], Bus_input[7], Y_shifted_input[7]);
  or or_9 (OR_output[8], Bus_input[8], Y_shifted_input[8]);
  or or_10 (OR_output[9], Bus_input[9], Y_shifted_input[9]);
  or or_11 (OR_output[10], Bus_input[10], Y_shifted_input[10]);
  or or_12 (OR_output[11], Bus_input[11], Y_shifted_input[11]);
  or or_13 (OR_output[12], Bus_input[12], Y_shifted_input[12]);
  or or_14 (OR_output[13], Bus_input[13], Y_shifted_input[13]);
  or or_15 (OR_output[14], Bus_input[14], Y_shifted_input[14]);
  or or_16 (OR_output[15], Bus_input[15], Y_shifted_input[15]);
endmodule

module logical_NOT_bus (
  input  [15:0] Bus_input,
  output [15:0] NOT_output
);

  not not_1 (NOT_output[0], Bus_input[0]);
  not not_2 (NOT_output[1], Bus_input[1]);
  not not_3 (NOT_output[2], Bus_input[2]);
  not not_4 (NOT_output[3], Bus_input[3]);
  not not_5 (NOT_output[4], Bus_input[4]);
  not not_6 (NOT_output[5], Bus_input[5]);
  not not_7 (NOT_output[6], Bus_input[6]);
  not not_8 (NOT_output[7], Bus_input[7]);
  not not_9 (NOT_output[8], Bus_input[8]);
  not not_10 (NOT_output[9], Bus_input[9]);
  not not_11 (NOT_output[10], Bus_input[10]);
  not not_12 (NOT_output[11], Bus_input[11]);
  not not_13 (NOT_output[12], Bus_input[12]);
  not not_14 (NOT_output[13], Bus_input[13]);
  not not_15 (NOT_output[14], Bus_input[14]);
  not not_16 (NOT_output[15], Bus_input[15]);
endmodule

module full_adder_1_bit (
  input  A,
  input  B,
  input  CarryIn,
  output Sum,
  output CarryOut
);

  wire and_1_out, and_2_out, xor_1_out;

  xor xor_1 (xor_1_out, A, B);
  and and_1 (and_1_out, B, A);
  xor xor_2 (Sum, xor_1_out, CarryIn);
  and and_2 (and_2_out, CarryIn, xor_1_out);
  or or_1 (CarryOut, and_2_out, and_1_out);
endmodule

module ADD_SUB_INC (
  input  [15:0] bus_input_or_2,
  input  [15:0] Y_shifted_input,
  input  ALU_subtract,
  output [15:0] ADDSUB_output
);

  wire full_adder_1_bit_2_carryout, full_adder_1_bit_3_carryout, full_adder_1_bit_4_carryout,
       full_adder_1_bit_5_carryout, full_adder_1_bit_6_carryout, full_adder_1_bit_7_carryout,
       full_adder_1_bit_8_carryout, full_adder_1_bit_9_carryout, full_adder_1_bit_10_carryout,
       full_adder_1_bit_11_carryout, full_adder_1_bit_12_carryout, full_adder_1_bit_13_carryout,
       full_adder_1_bit_14_carryout, full_adder_1_bit_15_carryout, full_adder_1_bit_16_carryout, xor_1_out,
       xor_2_out, xor_3_out, xor_4_out, xor_5_out, xor_6_out, xor_7_out, xor_8_out, xor_9_out, xor_10_out,
       xor_11_out, xor_12_out, xor_13_out, xor_14_out, xor_15_out, xor_16_out;

  xor xor_1 (xor_1_out, Y_shifted_input[0], ALU_subtract);
  xor xor_2 (xor_2_out, Y_shifted_input[1], ALU_subtract);
  xor xor_3 (xor_3_out, Y_shifted_input[2], ALU_subtract);
  xor xor_4 (xor_4_out, Y_shifted_input[3], ALU_subtract);
  xor xor_5 (xor_5_out, Y_shifted_input[4], ALU_subtract);
  xor xor_6 (xor_6_out, Y_shifted_input[5], ALU_subtract);
  xor xor_7 (xor_7_out, Y_shifted_input[6], ALU_subtract);
  xor xor_8 (xor_8_out, Y_shifted_input[7], ALU_subtract);
  xor xor_9 (xor_9_out, Y_shifted_input[8], ALU_subtract);
  xor xor_10 (xor_10_out, Y_shifted_input[9], ALU_subtract);
  xor xor_11 (xor_11_out, Y_shifted_input[10], ALU_subtract);
  xor xor_12 (xor_12_out, Y_shifted_input[11], ALU_subtract);
  xor xor_13 (xor_13_out, Y_shifted_input[12], ALU_subtract);
  xor xor_14 (xor_14_out, Y_shifted_input[13], ALU_subtract);
  xor xor_15 (xor_15_out, Y_shifted_input[14], ALU_subtract);
  xor xor_16 (xor_16_out, Y_shifted_input[15], ALU_subtract);
  full_adder_1_bit full_adder_1_bit_1 (
    .A(bus_input_or_2[0]), .B(xor_1_out), .CarryIn(full_adder_1_bit_2_carryout), .Sum(ADDSUB_output[0]));  // open: CarryOut
  full_adder_1_bit full_adder_1_bit_2 (
    .A(bus_input_or_2[1]), .B(xor_2_out), .CarryIn(full_adder_1_bit_3_carryout), .Sum(ADDSUB_output[1]),
    .CarryOut(full_adder_1_bit_2_carryout));
  full_adder_1_bit full_adder_1_bit_3 (
    .A(bus_input_or_2[2]), .B(xor_3_out), .CarryIn(full_adder_1_bit_4_carryout), .Sum(ADDSUB_output[2]),
    .CarryOut(full_adder_1_bit_3_carryout));
  full_adder_1_bit full_adder_1_bit_4 (
    .A(bus_input_or_2[3]), .B(xor_4_out), .CarryIn(full_adder_1_bit_5_carryout), .Sum(ADDSUB_output[3]),
    .CarryOut(full_adder_1_bit_4_carryout));
  full_adder_1_bit full_adder_1_bit_5 (
    .A(bus_input_or_2[4]), .B(xor_5_out), .CarryIn(full_adder_1_bit_6_carryout), .Sum(ADDSUB_output[4]),
    .CarryOut(full_adder_1_bit_5_carryout));
  full_adder_1_bit full_adder_1_bit_6 (
    .A(bus_input_or_2[5]), .B(xor_6_out), .CarryIn(full_adder_1_bit_7_carryout), .Sum(ADDSUB_output[5]),
    .CarryOut(full_adder_1_bit_6_carryout));
  full_adder_1_bit full_adder_1_bit_7 (
    .A(bus_input_or_2[6]), .B(xor_7_out), .CarryIn(full_adder_1_bit_8_carryout), .Sum(ADDSUB_output[6]),
    .CarryOut(full_adder_1_bit_7_carryout));
  full_adder_1_bit full_adder_1_bit_8 (
    .A(bus_input_or_2[7]), .B(xor_8_out), .CarryIn(full_adder_1_bit_9_carryout), .Sum(ADDSUB_output[7]),
    .CarryOut(full_adder_1_bit_8_carryout));
  full_adder_1_bit full_adder_1_bit_9 (
    .A(bus_input_or_2[8]), .B(xor_9_out), .CarryIn(full_adder_1_bit_10_carryout), .Sum(ADDSUB_output[8]),
    .CarryOut(full_adder_1_bit_9_carryout));
  full_adder_1_bit full_adder_1_bit_10 (
    .A(bus_input_or_2[9]), .B(xor_10_out), .CarryIn(full_adder_1_bit_11_carryout), .Sum(ADDSUB_output[9]),
    .CarryOut(full_adder_1_bit_10_carryout));
  full_adder_1_bit full_adder_1_bit_11 (
    .A(bus_input_or_2[10]), .B(xor_11_out), .CarryIn(full_adder_1_bit_12_carryout), .Sum(ADDSUB_output[10]),
    .CarryOut(full_adder_1_bit_11_carryout));
  full_adder_1_bit full_adder_1_bit_12 (
    .A(bus_input_or_2[11]), .B(xor_12_out), .CarryIn(full_adder_1_bit_13_carryout), .Sum(ADDSUB_output[11]),
    .CarryOut(full_adder_1_bit_12_carryout));
  full_adder_1_bit full_adder_1_bit_13 (
    .A(bus_input_or_2[12]), .B(xor_13_out), .CarryIn(full_adder_1_bit_14_carryout), .Sum(ADDSUB_output[12]),
    .CarryOut(full_adder_1_bit_13_carryout));
  full_adder_1_bit full_adder_1_bit_14 (
    .A(bus_input_or_2[13]), .B(xor_14_out), .CarryIn(full_adder_1_bit_15_carryout), .Sum(ADDSUB_output[13]),
    .CarryOut(full_adder_1_bit_14_carryout));
  full_adder_1_bit full_adder_1_bit_15 (
    .A(bus_input_or_2[14]), .B(xor_15_out), .CarryIn(full_adder_1_bit_16_carryout), .Sum(ADDSUB_output[14]),
    .CarryOut(full_adder_1_bit_15_carryout));
  full_adder_1_bit full_adder_1_bit_16 (
    .A(bus_input_or_2[15]), .B(xor_16_out), .CarryIn(ALU_subtract), .Sum(ADDSUB_output[15]),
    .CarryOut(full_adder_1_bit_16_carryout));
endmodule

module ALU (
  input  [2:0] ALU_control,
  input  [15:0] bus_input,
  input  [15:0] Y_shifted_input,
  output [15:0] ALU_out
);

  wire decoder_1_out0, decoder_1_out1, decoder_1_out2, decoder_1_out3, decoder_1_out4, decoder_1_out5,
       decoder_1_out6, not_2_out, or_1_out;
  wire [15:0] add_sub_inc_1_addsub_output, controlled_buffer_1_out, logical_and_1_and_output,
       logical_not_bus_1_not_output, logical_or_1_or_output;
  wire [15:1] not_1_out;

  not not_1 (not_1_out[1], not_1_out[15]);
  not not_2 (not_2_out, decoder_1_out2);
  assign controlled_buffer_1_out = not_2_out ? bus_input : 16'bz;  // Controlled_Buffer controlled_buffer_1
  assign controlled_buffer_1_out = decoder_1_out2 ? {{14{not_1_out[15]}}, not_1_out[1], not_1_out[15]} : 16'bz;  // Controlled_Buffer controlled_buffer_2
  Decoder #(.enable("false"), .select(3)) decoder_1 (
    .out0(decoder_1_out0), .out1(decoder_1_out1), .out2(decoder_1_out2), .out3(decoder_1_out3),
    .out4(decoder_1_out4), .out5(decoder_1_out5), .out6(decoder_1_out6), .out7(not_1_out[15]),
    .sel(ALU_control));
  or or_1 (or_1_out, decoder_1_out0, decoder_1_out2, decoder_1_out6);
  assign ALU_out = decoder_1_out1 ? logical_and_1_and_output : 16'bz;  // Controlled_Buffer controlled_buffer_3
  logical_AND logical_and_1 (
    .Bus_input(bus_input), .Y_shifted_input(Y_shifted_input), .AND_output(logical_and_1_and_output));
  assign ALU_out = decoder_1_out4 ? logical_or_1_or_output : 16'bz;  // Controlled_Buffer controlled_buffer_4
  logical_OR logical_or_1 (
    .Bus_input(bus_input), .Y_shifted_input(Y_shifted_input), .OR_output(logical_or_1_or_output));
  assign ALU_out = decoder_1_out3 ? logical_not_bus_1_not_output : 16'bz;  // Controlled_Buffer controlled_buffer_5
  logical_NOT_bus logical_not_bus_1 (.Bus_input(bus_input), .NOT_output(logical_not_bus_1_not_output));
  assign ALU_out = decoder_1_out5 ? Y_shifted_input : 16'bz;  // Controlled_Buffer controlled_buffer_6
  assign ALU_out = or_1_out ? add_sub_inc_1_addsub_output : 16'bz;  // Controlled_Buffer controlled_buffer_7
  ADD_SUB_INC add_sub_inc_1 (
    .bus_input_or_2(controlled_buffer_1_out), .Y_shifted_input(Y_shifted_input),
    .ALU_subtract(decoder_1_out6), .ADDSUB_output(add_sub_inc_1_addsub_output));
endmodule

module Comp_arator (
  input  [15:0] from_ALU,
  output CC_Z,
  output CC_N
);

  nor nor_1 (CC_Z, from_ALU[0], from_ALU[1], from_ALU[2], from_ALU[3], from_ALU[4], from_ALU[5], from_ALU[6], from_ALU[7], from_ALU[8], from_ALU[9], from_ALU[10], from_ALU[11], from_ALU[12], from_ALU[13], from_ALU[14], from_ALU[15]);

  assign CC_N = from_ALU[15];
endmodule

module control_unit (
  input  [3:0] IR_opcode,
  input  [2:0] PSW_0_1_2,
  input  [2:0] IR_Rs2,
  input  TIMEOUT,
  output [2:0] ALU_control,
  output Clck,
  output GPR_in,
  output GPR_out,
  output [2:0] GPR_select,
  output IR_in,
  output Load_MM,
  output MAR_in,
  output MDR_in,
  output MDR_out,
  output PSW_in,
  output PSW_out,
  output Read_MM,
  output ROM_8_out,
  output Timer_In,
  output Y_in,
  output Y_offset_in,
  output Y_out,
  output Y_shift_left,
  output Y_shift_right,
  output Z_in,
  output Z_out
);

  wire and_1_out, and_2_out, and_3_out, and_4_out, and_5_out, and_6_out, and_7_out, and_8_out, and_9_out,
       and_10_out, and_11_out, and_12_out, and_13_out, and_14_out, and_15_out, and_16_out, and_17_out,
       and_18_out, and_19_out, and_20_out, and_21_out, and_22_out, and_23_out, and_24_out, and_25_out,
       and_26_out, and_27_out, and_28_out, and_29_out, and_30_out, and_31_out, and_32_out, and_33_out,
       and_34_out, and_35_out, and_36_out, and_37_out, and_38_out, and_39_out, and_40_out, and_41_out,
       and_42_out, and_43_out, and_44_out, and_45_out, and_46_out, and_47_out, and_48_out, and_49_out,
       and_50_out, and_51_out, and_52_out, and_53_out, and_54_out, and_55_out, nor_1_out, not_1_out,
       not_2_out, not_3_out, not_4_out, not_5_out, not_6_out, not_7_out, not_8_out, or_1_out, or_2_out,
       or_3_out, or_4_out, or_5_out, or_6_out, or_7_out, or_8_out, or_9_out, or_10_out, or_11_out, or_12_out,
       or_13_out, or_14_out, or_15_out, or_16_out, or_17_out, or_18_out, or_19_out, or_20_out, or_21_out,
       or_22_out, or_23_out, or_24_out, or_25_out, or_26_out, or_29_out, or_30_out, or_31_out;
  wire [4:0] D4_q;
  wire [15:0] decoder_1_out0;
  wire [31:0] decoder_2_out0;

  Decoder #(.enable("false"), .select(4)) decoder_1 (
    .out0(decoder_1_out0[0]), .out1(decoder_1_out0[1]), .out2(decoder_1_out0[2]), .out3(decoder_1_out0[3]),
    .out4(decoder_1_out0[4]), .out5(decoder_1_out0[5]), .out6(decoder_1_out0[6]), .out7(decoder_1_out0[7]),
    .out8(decoder_1_out0[8]), .out9(decoder_1_out0[9]), .out10(decoder_1_out0[10]),
    .out11(decoder_1_out0[11]), .out12(decoder_1_out0[12]), .out13(decoder_1_out0[13]),
    .out14(decoder_1_out0[14]), .out15(decoder_1_out0[15]), .sel(IR_opcode));
  nor nor_1 (nor_1_out, IR_Rs2[0], IR_Rs2[1], IR_Rs2[2]);
  not not_1 (not_1_out, nor_1_out);
  not not_2 (not_2_out, PSW_0_1_2[2]);
  or or_1 (or_1_out, decoder_1_out0[14], decoder_1_out0[15]);
  not not_3 (not_3_out, PSW_0_1_2[2]);
  not not_4 (not_4_out, PSW_0_1_2[2]);
  or or_2 (or_2_out, decoder_1_out0[14], decoder_1_out0[15]);
  not not_5 (not_5_out, nor_1_out);
  not not_6 (not_6_out, PSW_0_1_2[2]);
  or or_3 (or_3_out, decoder_1_out0[14], decoder_1_out0[15]);
  not not_7 (not_7_out, PSW_0_1_2[2]);
  and and_1 (and_1_out, decoder_1_out0[5], nor_1_out);
  and and_2 (and_2_out, decoder_1_out0[5], not_1_out);
  and and_3 (and_3_out, not_2_out, or_1_out);
  or or_4 (or_4_out, PSW_0_1_2[2], and_4_out);
  and and_4 (and_4_out, not_3_out, TIMEOUT);
  and and_5 (and_5_out, decoder_2_out0[5], decoder_1_out0[13]);
  and and_6 (and_6_out, decoder_2_out0[5], decoder_1_out0[6]);
  and and_7 (and_7_out, decoder_2_out0[2], decoder_1_out0[7]);
  and and_8 (and_8_out, decoder_2_out0[2], decoder_1_out0[8]);
  and and_9 (and_9_out, decoder_2_out0[2], decoder_1_out0[14]);
  and and_10 (and_10_out, decoder_2_out0[2], decoder_1_out0[15]);
  and and_11 (and_11_out, decoder_2_out0[4], decoder_1_out0[0]);
  or or_5 (or_5_out, decoder_2_out0[15], ROM_8_out, decoder_2_out0[17], decoder_2_out0[18], decoder_2_out0[19], decoder_2_out0[20], decoder_2_out0[21]);
  or or_6 (or_6_out, Y_shift_right, decoder_2_out0[23], PSW_out, decoder_2_out0[25], decoder_2_out0[26], decoder_2_out0[27], decoder_2_out0[28], decoder_2_out0[29]);
  or or_7 (or_7_out, IR_in, decoder_2_out0[6], decoder_2_out0[27], decoder_2_out0[28], decoder_2_out0[29]);
  and and_12 (and_12_out, decoder_2_out0[2], decoder_1_out0[8]);
  and and_13 (and_13_out, decoder_2_out0[2], decoder_1_out0[14]);
  and and_14 (and_14_out, decoder_2_out0[2], decoder_1_out0[15]);
  and and_15 (and_15_out, decoder_2_out0[4], decoder_1_out0[0]);
  or or_8 (or_8_out, decoder_1_out0[0], decoder_1_out0[1], decoder_1_out0[2], decoder_1_out0[3]);
  or or_9 (or_9_out, decoder_1_out0[14], decoder_1_out0[15]);
  and and_16 (and_16_out, or_9_out, not_4_out);
  or or_10 (or_10_out, decoder_2_out0[0], decoder_2_out0[6], decoder_2_out0[25], decoder_2_out0[26], decoder_2_out0[29]);
  and and_17 (and_17_out, PSW_0_1_2[2], or_2_out);
  or or_11 (or_11_out, and_17_out, decoder_1_out0[8], decoder_1_out0[7]);
  and and_18 (and_18_out, decoder_1_out0[5], not_5_out);
  and and_19 (and_19_out, not_6_out, or_3_out);
  or or_12 (or_12_out, decoder_2_out0[0], IR_in, decoder_2_out0[6], PSW_out, decoder_2_out0[26], decoder_2_out0[28]);
  and and_20 (and_20_out, decoder_1_out0[9], PSW_0_1_2[1]);
  and and_21 (and_21_out, decoder_1_out0[10], PSW_0_1_2[0]);
  or or_13 (or_13_out, decoder_2_out0[7], decoder_2_out0[9]);
  and and_22 (and_22_out, decoder_1_out0[5], nor_1_out);
  or or_14 (or_14_out, decoder_1_out0[14], decoder_1_out0[15]);
  and and_23 (and_23_out, or_14_out, not_7_out);
  and and_24 (and_24_out, decoder_2_out0[4], decoder_1_out0[1]);
  and and_25 (and_25_out, decoder_2_out0[4], decoder_1_out0[2]);
  and and_26 (and_26_out, decoder_2_out0[4], decoder_1_out0[3]);
  and and_27 (and_27_out, decoder_2_out0[5], decoder_1_out0[4]);
  and and_28 (and_28_out, decoder_2_out0[5], and_1_out);
  and and_29 (and_29_out, decoder_2_out0[5], and_2_out);
  and and_30 (and_30_out, decoder_2_out0[5], and_3_out);
  or or_15 (or_15_out, decoder_2_out0[1], decoder_2_out0[8], decoder_2_out0[10], decoder_2_out0[11], decoder_2_out0[12], Timer_In, decoder_2_out0[14]);
  not not_8 (not_8_out, or_4_out);
  or or_16 (or_16_out, or_5_out, or_6_out);
  and and_31 (and_31_out, decoder_2_out0[5], decoder_1_out0[12]);
  and and_32 (and_32_out, decoder_2_out0[5], or_8_out);
  and and_33 (and_33_out, decoder_2_out0[5], decoder_1_out0[4]);
  and and_34 (and_34_out, decoder_2_out0[5], decoder_1_out0[5]);
  and and_35 (and_35_out, decoder_2_out0[5], and_16_out);
  and and_36 (and_36_out, decoder_2_out0[5], decoder_1_out0[12]);
  and and_37 (and_37_out, decoder_2_out0[5], decoder_1_out0[6]);
  and and_38 (and_38_out, decoder_2_out0[5], or_11_out);
  and and_39 (and_39_out, decoder_2_out0[5], and_18_out);
  and and_40 (and_40_out, decoder_2_out0[5], and_19_out);
  and and_41 (and_41_out, decoder_2_out0[2], decoder_1_out0[7]);
  and and_42 (and_42_out, decoder_2_out0[2], decoder_1_out0[15]);
  and and_43 (and_43_out, decoder_2_out0[4], decoder_1_out0[0]);
  and and_44 (and_44_out, decoder_2_out0[4], decoder_1_out0[2]);
  and and_45 (and_45_out, decoder_2_out0[4], decoder_1_out0[4]);
  or or_17 (or_17_out, decoder_1_out0[11], and_20_out, and_21_out);
  and and_46 (and_46_out, or_15_out, not_8_out);
  or or_18 (or_18_out, and_46_out, ROM_8_out, decoder_2_out0[23], PSW_out, decoder_2_out0[25], decoder_2_out0[26], decoder_2_out0[27], decoder_2_out0[28], decoder_2_out0[29]);
  or or_19 (or_19_out, and_5_out, and_6_out, and_7_out, and_8_out, and_9_out, and_10_out, and_11_out, or_16_out);
  and and_47 (and_47_out, decoder_2_out0[5], or_17_out);
  and and_48 (and_48_out, decoder_2_out0[5], decoder_1_out0[13]);
  and and_49 (and_49_out, decoder_2_out0[5], and_22_out);
  and and_50 (and_50_out, decoder_2_out0[5], and_23_out);
  and and_51 (and_51_out, decoder_2_out0[2], decoder_1_out0[7]);
  and and_52 (and_52_out, decoder_2_out0[2], decoder_1_out0[14]);
  and and_53 (and_53_out, decoder_2_out0[4], decoder_1_out0[0]);
  and and_54 (and_54_out, decoder_2_out0[4], decoder_1_out0[1]);
  and and_55 (and_55_out, decoder_2_out0[4], decoder_1_out0[3]);
  or or_20 (or_20_out, or_7_out, and_12_out, and_13_out, and_14_out, and_15_out, and_31_out, and_32_out, and_33_out, and_34_out, and_35_out);
  or or_21 (or_21_out, or_10_out, and_36_out, and_37_out, and_38_out, and_39_out, and_40_out, and_41_out, and_42_out, and_43_out, and_44_out, and_45_out);
  or or_22 (or_22_out, or_12_out, and_47_out, or_13_out, and_48_out, and_49_out, and_50_out, and_51_out, and_52_out, and_53_out, and_54_out, and_55_out);
  Clock clock_1 (.out(Clck));
  or or_23 (or_23_out, and_24_out, and_25_out, and_26_out, and_27_out, and_28_out, and_29_out, and_30_out, or_18_out);
  D_Flip_Flop D0 (.D(or_23_out), .clk(Clck), .Q(D4_q[4]));  // open: Qn, preset, reset
  D_Flip_Flop D1 (.D(or_19_out), .clk(Clck), .Q(D4_q[3]));  // open: Qn, preset, reset
  D_Flip_Flop D2 (.D(or_20_out), .clk(Clck), .Q(D4_q[2]));  // open: Qn, preset, reset
  D_Flip_Flop D3 (.D(or_21_out), .clk(Clck), .Q(D4_q[1]));  // open: Qn, preset, reset
  D_Flip_Flop D4 (.D(or_22_out), .clk(Clck), .Q(D4_q[0]));  // open: Qn, preset, reset
  Decoder #(.enable("false"), .select(5)) decoder_2 (
    .out0(decoder_2_out0[0]), .out1(decoder_2_out0[1]), .out2(decoder_2_out0[2]), .out3(IR_in),
    .out4(decoder_2_out0[4]), .out5(decoder_2_out0[5]), .out6(decoder_2_out0[6]), .out7(decoder_2_out0[7]),
    .out8(decoder_2_out0[8]), .out9(decoder_2_out0[9]), .out10(decoder_2_out0[10]),
    .out11(decoder_2_out0[11]), .out12(decoder_2_out0[12]), .out13(Timer_In), .out14(decoder_2_out0[14]),
    .out15(decoder_2_out0[15]), .out16(ROM_8_out), .out17(decoder_2_out0[17]), .out18(decoder_2_out0[18]),
    .out19(decoder_2_out0[19]), .out20(decoder_2_out0[20]), .out21(decoder_2_out0[21]),
    .out22(Y_shift_right), .out23(decoder_2_out0[23]), .out24(PSW_out), .out25(decoder_2_out0[25]),
    .out26(decoder_2_out0[26]), .out27(decoder_2_out0[27]), .out28(decoder_2_out0[28]),
    .out29(decoder_2_out0[29]), .out30(decoder_2_out0[30]), .out31(decoder_2_out0[31]), .sel(D4_q));
  or or_24 (or_24_out, decoder_2_out0[5], decoder_2_out0[9], decoder_2_out0[15]);
  or or_25 (or_25_out, decoder_2_out0[0], PSW_out, decoder_2_out0[26], decoder_2_out0[28]);
  or or_26 (or_26_out, decoder_2_out0[21], Y_shift_right);
  or or_27 (GPR_in, decoder_2_out0[5], decoder_2_out0[1], decoder_2_out0[7], decoder_2_out0[10], decoder_2_out0[11], decoder_2_out0[30], decoder_2_out0[8]);
  or or_28 (GPR_out, decoder_2_out0[0], decoder_2_out0[6], decoder_2_out0[9], decoder_2_out0[12], decoder_2_out0[23], decoder_2_out0[26], decoder_2_out0[4], decoder_2_out0[15], decoder_2_out0[17], decoder_2_out0[18], decoder_2_out0[19], decoder_2_out0[20], decoder_2_out0[21], Y_shift_right);
  or or_29 (or_29_out, decoder_2_out0[0], decoder_2_out0[5], decoder_2_out0[1], decoder_2_out0[6], decoder_2_out0[26], decoder_2_out0[30]);
  or or_30 (or_30_out, decoder_2_out0[7], decoder_2_out0[9], decoder_2_out0[10], decoder_2_out0[11], decoder_2_out0[12]);
  or or_31 (or_31_out, decoder_2_out0[15], decoder_2_out0[17], decoder_2_out0[18], decoder_2_out0[19], decoder_2_out0[20], decoder_2_out0[21], Y_shift_right);
  or or_32 (Load_MM, decoder_2_out0[12], PSW_out, decoder_2_out0[26]);
  or or_33 (MAR_in, decoder_2_out0[0], decoder_2_out0[2], decoder_2_out0[23], decoder_2_out0[25], decoder_2_out0[27], decoder_2_out0[29], ROM_8_out);
  or or_34 (MDR_out, IR_in, decoder_2_out0[11], Timer_In, decoder_2_out0[14], decoder_2_out0[28], decoder_2_out0[30]);
  or or_35 (PSW_in, decoder_2_out0[14], decoder_2_out0[28]);
  or or_36 (Read_MM, decoder_2_out0[0], decoder_2_out0[2], decoder_2_out0[27], decoder_2_out0[29]);
  or or_37 (Y_in, decoder_2_out0[0], decoder_2_out0[6], decoder_2_out0[23], decoder_2_out0[25], decoder_2_out0[27], ROM_8_out, decoder_2_out0[4], decoder_2_out0[21], Y_shift_right);
  or or_38 (Y_out, decoder_2_out0[7], decoder_2_out0[10]);
  or or_39 (Y_shift_left, decoder_2_out0[15], decoder_2_out0[17], decoder_2_out0[18], decoder_2_out0[19], decoder_2_out0[21]);
  or or_40 (Z_in, decoder_2_out0[0], decoder_2_out0[5], decoder_2_out0[9], PSW_out, decoder_2_out0[26], decoder_2_out0[28], decoder_2_out0[15], decoder_2_out0[17], decoder_2_out0[18], decoder_2_out0[19], decoder_2_out0[20], decoder_2_out0[21], Y_shift_right);
  or or_41 (Z_out, decoder_2_out0[5], decoder_2_out0[1], decoder_2_out0[25], decoder_2_out0[27], decoder_2_out0[29], decoder_2_out0[8]);
  Priority_Encoder priority_encoder_1 (
    .in0(decoder_2_out0[23]), .in1(or_29_out), .in2(decoder_2_out0[8]), .in3(or_30_out), .in4(or_31_out),
    .in5(decoder_2_out0[4]), .out(GPR_select));  // open: in6, in7, en_in, gs, en_out
  Priority_Encoder priority_encoder_2 (
    .in0(or_24_out), .in1(decoder_2_out0[18]), .in2(or_25_out), .in3(decoder_2_out0[8]),
    .in4(decoder_2_out0[19]), .in5(or_26_out), .in6(decoder_2_out0[17]), .out(ALU_control));  // open: in7, en_in, gs, en_out

  assign MDR_in = Load_MM;
  assign Y_offset_in = IR_in;
endmodule

module GPR (
  input  [15:0] BUS_in,
  input  GPR_in,
  input  GPR_out,
  output [15:0] BUS_out
);

  wire [15:0] d_ff_1_q;

  D_Flip_Flop d_ff_1 (.D(BUS_in[0]), .clk(GPR_in), .Q(d_ff_1_q[0]));  // open: Qn, preset, reset
  D_Flip_Flop d_ff_2 (.D(BUS_in[1]), .clk(GPR_in), .Q(d_ff_1_q[1]));  // open: Qn, preset, reset
  D_Flip_Flop d_ff_3 (.D(BUS_in[2]), .clk(GPR_in), .Q(d_ff_1_q[2]));  // open: Qn, preset, reset
  D_Flip_Flop d_ff_4 (.D(BUS_in[3]), .clk(GPR_in), .Q(d_ff_1_q[3]));  // open: Qn, preset, reset
  D_Flip_Flop d_ff_5 (.D(BUS_in[4]), .clk(GPR_in), .Q(d_ff_1_q[4]));  // open: Qn, preset, reset
  D_Flip_Flop d_ff_6 (.D(BUS_in[5]), .clk(GPR_in), .Q(d_ff_1_q[5]));  // open: Qn, preset, reset
  D_Flip_Flop d_ff_7 (.D(BUS_in[6]), .clk(GPR_in), .Q(d_ff_1_q[6]));  // open: Qn, preset, reset
  D_Flip_Flop d_ff_8 (.D(BUS_in[7]), .clk(GPR_in), .Q(d_ff_1_q[7]));  // open: Qn, preset, reset
  D_Flip_Flop d_ff_9 (.D(BUS_in[8]), .clk(GPR_in), .Q(d_ff_1_q[8]));  // open: Qn, preset, reset
  D_Flip_Flop d_ff_10 (.D(BUS_in[9]), .clk(GPR_in), .Q(d_ff_1_q[9]));  // open: Qn, preset, reset
  D_Flip_Flop d_ff_11 (.D(BUS_in[10]), .clk(GPR_in), .Q(d_ff_1_q[10]));  // open: Qn, preset, reset
  D_Flip_Flop d_ff_12 (.D(BUS_in[11]), .clk(GPR_in), .Q(d_ff_1_q[11]));  // open: Qn, preset, reset
  D_Flip_Flop d_ff_13 (.D(BUS_in[12]), .clk(GPR_in), .Q(d_ff_1_q[12]));  // open: Qn, preset, reset
  D_Flip_Flop d_ff_14 (.D(BUS_in[13]), .clk(GPR_in), .Q(d_ff_1_q[13]));  // open: Qn, preset, reset
  D_Flip_Flop d_ff_15 (.D(BUS_in[14]), .clk(GPR_in), .Q(d_ff_1_q[14]));  // open: Qn, preset, reset
  D_Flip_Flop d_ff_16 (.D(BUS_in[15]), .clk(GPR_in), .Q(d_ff_1_q[15]));  // open: Qn, preset, reset
  assign BUS_out = GPR_out ? d_ff_1_q : 16'bz;  // Controlled_Buffer controlled_buffer_1
endmodule

module GPR_Full (
  input  [2:0] Rd_1,
  input  [2:0] Rd_2,
  input  [2:0] Rs_1,
  input  [2:0] Rs_2,
  input  GPR_in,
  input  GPR_out,
  input  [15:0] BUS_in,
  input  [2:0] GPR_sel,
  output [15:0] BUS_out
);

  wire and_1_out, and_2_out, and_3_out, and_4_out, and_5_out, and_6_out, and_7_out, and_8_out, and_9_out,
       and_10_out, and_11_out, and_12_out, and_13_out, and_14_out, and_15_out, and_16_out, decoder_1_out0,
       decoder_1_out1, decoder_1_out2, decoder_1_out3, decoder_1_out4, decoder_1_out5, decoder_1_out6,
       decoder_1_out7;
  wire [2:0] multiplexer_1_out;

  Multiplexer #(.select(3), .width(3)) multiplexer_1 (
    .in0(3'b000), .in1(3'b111), .in2(Rd_1), .in3(Rd_2), .in4(Rs_1), .in5(Rs_2), .out(multiplexer_1_out),
    .sel(GPR_sel));  // open: in6, in7
  Decoder #(.enable("false"), .select(3)) decoder_1 (
    .out0(decoder_1_out0), .out1(decoder_1_out1), .out2(decoder_1_out2), .out3(decoder_1_out3),
    .out4(decoder_1_out4), .out5(decoder_1_out5), .out6(decoder_1_out6), .out7(decoder_1_out7),
    .sel(multiplexer_1_out));
  and and_1 (and_1_out, GPR_in, decoder_1_out0);
  and and_2 (and_2_out, GPR_out, decoder_1_out0);
  and and_3 (and_3_out, GPR_in, decoder_1_out1);
  and and_4 (and_4_out, GPR_out, decoder_1_out1);
  and and_5 (and_5_out, GPR_in, decoder_1_out2);
  and and_6 (and_6_out, GPR_out, decoder_1_out2);
  and and_7 (and_7_out, GPR_in, decoder_1_out3);
  and and_8 (and_8_out, GPR_out, decoder_1_out3);
  and and_9 (and_9_out, GPR_in, decoder_1_out4);
  and and_10 (and_10_out, GPR_out, decoder_1_out4);
  and and_11 (and_11_out, GPR_in, decoder_1_out5);
  and and_12 (and_12_out, GPR_out, decoder_1_out5);
  and and_13 (and_13_out, GPR_in, decoder_1_out6);
  and and_14 (and_14_out, GPR_out, decoder_1_out6);
  and and_15 (and_15_out, GPR_in, decoder_1_out7);
  and and_16 (and_16_out, GPR_out, decoder_1_out7);
  GPR R0 (.BUS_in(BUS_in), .GPR_in(and_1_out), .GPR_out(and_2_out), .BUS_out(BUS_out));
  GPR R1 (.BUS_in(BUS_in), .GPR_in(and_3_out), .GPR_out(and_4_out), .BUS_out(BUS_out));
  GPR R2 (.BUS_in(BUS_in), .GPR_in(and_5_out), .GPR_out(and_6_out), .BUS_out(BUS_out));
  GPR R3 (.BUS_in(BUS_in), .GPR_in(and_7_out), .GPR_out(and_8_out), .BUS_out(BUS_out));
  GPR R4 (.BUS_in(BUS_in), .GPR_in(and_9_out), .GPR_out(and_10_out), .BUS_out(BUS_out));
  GPR R5 (.BUS_in(BUS_in), .GPR_in(and_11_out), .GPR_out(and_12_out), .BUS_out(BUS_out));
  GPR R6 (.BUS_in(BUS_in), .GPR_in(and_13_out), .GPR_out(and_14_out), .BUS_out(BUS_out));
  GPR R7 (.BUS_in(BUS_in), .GPR_in(and_15_out), .GPR_out(and_16_out), .BUS_out(BUS_out));
endmodule

module IR (
  input  [15:0] BUS_in,
  input  IR_in,
  output [2:0] Rd_out_2,
  output [2:0] Rs1,
  output [2:0] Rs2,
  output [2:0] Rd_out_1,
  output [3:0] OPCODE_out,
  output S,
  output [1:0] Shift
);

  D_Flip_Flop d_ff_1 (.D(BUS_in[0]), .clk(IR_in), .Q(OPCODE_out[3]));  // open: Qn, preset, reset
  D_Flip_Flop d_ff_2 (.D(BUS_in[1]), .clk(IR_in), .Q(OPCODE_out[2]));  // open: Qn, preset, reset
  D_Flip_Flop d_ff_3 (.D(BUS_in[2]), .clk(IR_in), .Q(OPCODE_out[1]));  // open: Qn, preset, reset
  D_Flip_Flop d_ff_4 (.D(BUS_in[3]), .clk(IR_in), .Q(OPCODE_out[0]));  // open: Qn, preset, reset
  D_Flip_Flop d_ff_5 (.D(BUS_in[4]), .clk(IR_in), .Q(Rd_out_2[2]));  // open: Qn, preset, reset
  D_Flip_Flop d_ff_6 (.D(BUS_in[5]), .clk(IR_in), .Q(Rd_out_2[1]));  // open: Qn, preset, reset
  D_Flip_Flop d_ff_7 (.D(BUS_in[6]), .clk(IR_in), .Q(Rd_out_2[0]));  // open: Qn, preset, reset
  D_Flip_Flop d_ff_8 (.D(BUS_in[7]), .clk(IR_in), .Q(Rd_out_1[2]));  // open: Qn, preset, reset
  D_Flip_Flop d_ff_9 (.D(BUS_in[8]), .clk(IR_in), .Q(Rd_out_1[1]));  // open: Qn, preset, reset
  D_Flip_Flop d_ff_10 (.D(BUS_in[9]), .clk(IR_in), .Q(Rd_out_1[0]));  // open: Qn, preset, reset
  D_Flip_Flop d_ff_11 (.D(BUS_in[10]), .clk(IR_in), .Q(Rs1[2]));  // open: Qn, preset, reset
  D_Flip_Flop d_ff_12 (.D(BUS_in[11]), .clk(IR_in), .Q(Rs1[1]));  // open: Qn, preset, reset
  D_Flip_Flop d_ff_13 (.D(BUS_in[12]), .clk(IR_in), .Q(Rs1[0]));  // open: Qn, preset, reset
  D_Flip_Flop d_ff_14 (.D(BUS_in[13]), .clk(IR_in), .Q(Rs2[2]));  // open: Qn, preset, reset
  D_Flip_Flop d_ff_15 (.D(BUS_in[14]), .clk(IR_in), .Q(Rs2[1]));  // open: Qn, preset, reset
  D_Flip_Flop d_ff_16 (.D(BUS_in[15]), .clk(IR_in), .Q(Rs2[0]));  // open: Qn, preset, reset

  assign S = Rd_out_2[2];
  assign Shift = Rd_out_2[1:0];
endmodule

module MAR (
  input  [15:0] BUS_in,
  input  MAR_in,
  input  Read_MM,
  input  Load_MM,
  output [15:0] To_MM
);

  wire d_ff_1_q, d_ff_2_q, d_ff_3_q, d_ff_4_q, d_ff_5_q, d_ff_6_q, d_ff_7_q, d_ff_8_q, d_ff_9_q, d_ff_10_q,
       d_ff_11_q, d_ff_12_q, d_ff_13_q, d_ff_14_q, d_ff_15_q, d_ff_16_q, xor_1_out;

  D_Flip_Flop d_ff_1 (.D(BUS_in[0]), .clk(MAR_in), .Q(d_ff_1_q));  // open: Qn, preset, reset
  D_Flip_Flop d_ff_2 (.D(BUS_in[1]), .clk(MAR_in), .Q(d_ff_2_q));  // open: Qn, preset, reset
  D_Flip_Flop d_ff_3 (.D(BUS_in[2]), .clk(MAR_in), .Q(d_ff_3_q));  // open: Qn, preset, reset
  D_Flip_Flop d_ff_4 (.D(BUS_in[3]), .clk(MAR_in), .Q(d_ff_4_q));  // open: Qn, preset, reset
  D_Flip_Flop d_ff_5 (.D(BUS_in[4]), .clk(MAR_in), .Q(d_ff_5_q));  // open: Qn, preset, reset
  D_Flip_Flop d_ff_6 (.D(BUS_in[5]), .clk(MAR_in), .Q(d_ff_6_q));  // open: Qn, preset, reset
  D_Flip_Flop d_ff_7 (.D(BUS_in[6]), .clk(MAR_in), .Q(d_ff_7_q));  // open: Qn, preset, reset
  D_Flip_Flop d_ff_8 (.D(BUS_in[7]), .clk(MAR_in), .Q(d_ff_8_q));  // open: Qn, preset, reset
  D_Flip_Flop d_ff_9 (.D(BUS_in[8]), .clk(MAR_in), .Q(d_ff_9_q));  // open: Qn, preset, reset
  D_Flip_Flop d_ff_10 (.D(BUS_in[9]), .clk(MAR_in), .Q(d_ff_10_q));  // open: Qn, preset, reset
  D_Flip_Flop d_ff_11 (.D(BUS_in[10]), .clk(MAR_in), .Q(d_ff_11_q));  // open: Qn, preset, reset
  D_Flip_Flop d_ff_12 (.D(BUS_in[11]), .clk(MAR_in), .Q(d_ff_12_q));  // open: Qn, preset, reset
  D_Flip_Flop d_ff_13 (.D(BUS_in[12]), .clk(MAR_in), .Q(d_ff_13_q));  // open: Qn, preset, reset
  D_Flip_Flop d_ff_14 (.D(BUS_in[13]), .clk(MAR_in), .Q(d_ff_14_q));  // open: Qn, preset, reset
  D_Flip_Flop d_ff_15 (.D(BUS_in[14]), .clk(MAR_in), .Q(d_ff_15_q));  // open: Qn, preset, reset
  D_Flip_Flop d_ff_16 (.D(BUS_in[15]), .clk(MAR_in), .Q(d_ff_16_q));  // open: Qn, preset, reset
  xor xor_1 (xor_1_out, Read_MM, Load_MM);
  assign To_MM[0] = xor_1_out ? d_ff_1_q : 1'bz;  // Controlled_Buffer controlled_buffer_1
  assign To_MM[1] = xor_1_out ? d_ff_2_q : 1'bz;  // Controlled_Buffer controlled_buffer_2
  assign To_MM[2] = xor_1_out ? d_ff_3_q : 1'bz;  // Controlled_Buffer controlled_buffer_3
  assign To_MM[3] = xor_1_out ? d_ff_4_q : 1'bz;  // Controlled_Buffer controlled_buffer_4
  assign To_MM[4] = xor_1_out ? d_ff_5_q : 1'bz;  // Controlled_Buffer controlled_buffer_5
  assign To_MM[5] = xor_1_out ? d_ff_6_q : 1'bz;  // Controlled_Buffer controlled_buffer_6
  assign To_MM[6] = xor_1_out ? d_ff_7_q : 1'bz;  // Controlled_Buffer controlled_buffer_7
  assign To_MM[7] = xor_1_out ? d_ff_8_q : 1'bz;  // Controlled_Buffer controlled_buffer_8
  assign To_MM[8] = xor_1_out ? d_ff_9_q : 1'bz;  // Controlled_Buffer controlled_buffer_9
  assign To_MM[9] = xor_1_out ? d_ff_10_q : 1'bz;  // Controlled_Buffer controlled_buffer_10
  assign To_MM[10] = xor_1_out ? d_ff_11_q : 1'bz;  // Controlled_Buffer controlled_buffer_11
  assign To_MM[11] = xor_1_out ? d_ff_12_q : 1'bz;  // Controlled_Buffer controlled_buffer_12
  assign To_MM[12] = xor_1_out ? d_ff_13_q : 1'bz;  // Controlled_Buffer controlled_buffer_13
  assign To_MM[13] = xor_1_out ? d_ff_14_q : 1'bz;  // Controlled_Buffer controlled_buffer_14
  assign To_MM[14] = xor_1_out ? d_ff_15_q : 1'bz;  // Controlled_Buffer controlled_buffer_15
  assign To_MM[15] = xor_1_out ? d_ff_16_q : 1'bz;  // Controlled_Buffer controlled_buffer_16
endmodule

module MDR_new (
  input  MDR_in,
  input  Read_MM,
  input  [15:0] BUS_in,
  input  MDR_out,
  input  Load_MM,
  input  [15:0] From_MM,
  output [15:0] BUS_out,
  output [15:0] To_MM
);

  wire and_1_out, and_2_out, and_3_out, and_4_out, and_5_out, and_6_out, and_7_out, and_8_out, and_9_out,
       and_10_out, and_11_out, and_12_out, and_13_out, and_14_out, and_15_out, and_16_out, and_17_out,
       and_18_out, and_19_out, and_20_out, and_21_out, and_22_out, and_23_out, and_24_out, and_25_out,
       and_26_out, and_27_out, and_28_out, and_29_out, and_30_out, and_31_out, and_32_out, d_ff_1_q,
       d_ff_2_q, d_ff_3_q, d_ff_4_q, d_ff_5_q, d_ff_6_q, d_ff_7_q, d_ff_8_q, d_ff_9_q, d_ff_10_q, d_ff_11_q,
       d_ff_12_q, d_ff_13_q, d_ff_14_q, d_ff_15_q, d_ff_16_q, or_1_out, or_2_out, or_3_out, or_4_out,
       or_5_out, or_6_out, or_7_out, or_8_out, or_9_out, or_10_out, or_11_out, or_12_out, or_13_out,
       or_14_out, or_15_out, or_16_out, xor_1_out;

  and and_1 (and_1_out, BUS_in[0], MDR_in);
  and and_2 (and_2_out, BUS_in[1], MDR_in);
  and and_3 (and_3_out, BUS_in[2], MDR_in);
  and and_4 (and_4_out, BUS_in[3], MDR_in);
  and and_5 (and_5_out, BUS_in[4], MDR_in);
  and and_6 (and_6_out, BUS_in[5], MDR_in);
  and and_7 (and_7_out, BUS_in[6], MDR_in);
  and and_8 (and_8_out, BUS_in[7], MDR_in);
  and and_9 (and_9_out, BUS_in[8], MDR_in);
  and and_10 (and_10_out, BUS_in[9], MDR_in);
  and and_11 (and_11_out, BUS_in[10], MDR_in);
  and and_12 (and_12_out, BUS_in[11], MDR_in);
  and and_13 (and_13_out, BUS_in[12], MDR_in);
  and and_14 (and_14_out, BUS_in[13], MDR_in);
  and and_15 (and_15_out, BUS_in[14], MDR_in);
  and and_16 (and_16_out, BUS_in[15], MDR_in);
  and and_17 (and_17_out, Read_MM, From_MM[0]);
  and and_18 (and_18_out, Read_MM, From_MM[1]);
  and and_19 (and_19_out, Read_MM, From_MM[2]);
  and and_20 (and_20_out, Read_MM, From_MM[3]);
  and and_21 (and_21_out, Read_MM, From_MM[4]);
  and and_22 (and_22_out, Read_MM, From_MM[5]);
  and and_23 (and_23_out, Read_MM, From_MM[6]);
  and and_24 (and_24_out, Read_MM, From_MM[7]);
  and and_25 (and_25_out, Read_MM, From_MM[8]);
  and and_26 (and_26_out, Read_MM, From_MM[9]);
  and and_27 (and_27_out, Read_MM, From_MM[10]);
  and and_28 (and_28_out, Read_MM, From_MM[11]);
  and and_29 (and_29_out, Read_MM, From_MM[12]);
  and and_30 (and_30_out, Read_MM, From_MM[13]);
  and and_31 (and_31_out, Read_MM, From_MM[14]);
  and and_32 (and_32_out, Read_MM, From_MM[15]);
  xor xor_1 (xor_1_out, MDR_in, Read_MM);
  or or_1 (or_1_out, and_17_out, and_1_out);
  or or_2 (or_2_out, and_18_out, and_2_out);
  or or_3 (or_3_out, and_19_out, and_3_out);
  or or_4 (or_4_out, and_20_out, and_4_out);
  or or_5 (or_5_out, and_21_out, and_5_out);
  or or_6 (or_6_out, and_22_out, and_6_out);
  or or_7 (or_7_out, and_23_out, and_7_out);
  or or_8 (or_8_out, and_24_out, and_8_out);
  or or_9 (or_9_out, and_25_out, and_9_out);
  or or_10 (or_10_out, and_26_out, and_10_out);
  or or_11 (or_11_out, and_27_out, and_11_out);
  or or_12 (or_12_out, and_28_out, and_12_out);
  or or_13 (or_13_out, and_29_out, and_13_out);
  or or_14 (or_14_out, and_30_out, and_14_out);
  or or_15 (or_15_out, and_31_out, and_15_out);
  or or_16 (or_16_out, and_32_out, and_16_out);
  D_Flip_Flop d_ff_1 (.D(or_1_out), .clk(xor_1_out), .Q(d_ff_1_q));  // open: Qn, preset, reset
  D_Flip_Flop d_ff_2 (.D(or_2_out), .clk(xor_1_out), .Q(d_ff_2_q));  // open: Qn, preset, reset
  D_Flip_Flop d_ff_3 (.D(or_3_out), .clk(xor_1_out), .Q(d_ff_3_q));  // open: Qn, preset, reset
  D_Flip_Flop d_ff_4 (.D(or_4_out), .clk(xor_1_out), .Q(d_ff_4_q));  // open: Qn, preset, reset
  D_Flip_Flop d_ff_5 (.D(or_5_out), .clk(xor_1_out), .Q(d_ff_5_q));  // open: Qn, preset, reset
  D_Flip_Flop d_ff_6 (.D(or_6_out), .clk(xor_1_out), .Q(d_ff_6_q));  // open: Qn, preset, reset
  D_Flip_Flop d_ff_7 (.D(or_7_out), .clk(xor_1_out), .Q(d_ff_7_q));  // open: Qn, preset, reset
  D_Flip_Flop d_ff_8 (.D(or_8_out), .clk(xor_1_out), .Q(d_ff_8_q));  // open: Qn, preset, reset
  D_Flip_Flop d_ff_9 (.D(or_9_out), .clk(xor_1_out), .Q(d_ff_9_q));  // open: Qn, preset, reset
  D_Flip_Flop d_ff_10 (.D(or_10_out), .clk(xor_1_out), .Q(d_ff_10_q));  // open: Qn, preset, reset
  D_Flip_Flop d_ff_11 (.D(or_11_out), .clk(xor_1_out), .Q(d_ff_11_q));  // open: Qn, preset, reset
  D_Flip_Flop d_ff_12 (.D(or_12_out), .clk(xor_1_out), .Q(d_ff_12_q));  // open: Qn, preset, reset
  D_Flip_Flop d_ff_13 (.D(or_13_out), .clk(xor_1_out), .Q(d_ff_13_q));  // open: Qn, preset, reset
  D_Flip_Flop d_ff_14 (.D(or_14_out), .clk(xor_1_out), .Q(d_ff_14_q));  // open: Qn, preset, reset
  D_Flip_Flop d_ff_15 (.D(or_15_out), .clk(xor_1_out), .Q(d_ff_15_q));  // open: Qn, preset, reset
  D_Flip_Flop d_ff_16 (.D(or_16_out), .clk(xor_1_out), .Q(d_ff_16_q));  // open: Qn, preset, reset
  assign To_MM[0] = Load_MM ? d_ff_1_q : 1'bz;  // Controlled_Buffer controlled_buffer_1
  assign To_MM[1] = Load_MM ? d_ff_2_q : 1'bz;  // Controlled_Buffer controlled_buffer_2
  assign To_MM[2] = Load_MM ? d_ff_3_q : 1'bz;  // Controlled_Buffer controlled_buffer_3
  assign To_MM[3] = Load_MM ? d_ff_4_q : 1'bz;  // Controlled_Buffer controlled_buffer_4
  assign To_MM[4] = Load_MM ? d_ff_5_q : 1'bz;  // Controlled_Buffer controlled_buffer_5
  assign To_MM[5] = Load_MM ? d_ff_6_q : 1'bz;  // Controlled_Buffer controlled_buffer_6
  assign To_MM[6] = Load_MM ? d_ff_7_q : 1'bz;  // Controlled_Buffer controlled_buffer_7
  assign To_MM[7] = Load_MM ? d_ff_8_q : 1'bz;  // Controlled_Buffer controlled_buffer_8
  assign To_MM[8] = Load_MM ? d_ff_9_q : 1'bz;  // Controlled_Buffer controlled_buffer_9
  assign To_MM[9] = Load_MM ? d_ff_10_q : 1'bz;  // Controlled_Buffer controlled_buffer_10
  assign To_MM[10] = Load_MM ? d_ff_11_q : 1'bz;  // Controlled_Buffer controlled_buffer_11
  assign To_MM[11] = Load_MM ? d_ff_12_q : 1'bz;  // Controlled_Buffer controlled_buffer_12
  assign To_MM[12] = Load_MM ? d_ff_13_q : 1'bz;  // Controlled_Buffer controlled_buffer_13
  assign To_MM[13] = Load_MM ? d_ff_14_q : 1'bz;  // Controlled_Buffer controlled_buffer_14
  assign To_MM[14] = Load_MM ? d_ff_15_q : 1'bz;  // Controlled_Buffer controlled_buffer_15
  assign To_MM[15] = Load_MM ? d_ff_16_q : 1'bz;  // Controlled_Buffer controlled_buffer_16
  assign BUS_out[0] = MDR_out ? d_ff_1_q : 1'bz;  // Controlled_Buffer controlled_buffer_17
  assign BUS_out[1] = MDR_out ? d_ff_2_q : 1'bz;  // Controlled_Buffer controlled_buffer_18
  assign BUS_out[2] = MDR_out ? d_ff_3_q : 1'bz;  // Controlled_Buffer controlled_buffer_19
  assign BUS_out[3] = MDR_out ? d_ff_4_q : 1'bz;  // Controlled_Buffer controlled_buffer_20
  assign BUS_out[4] = MDR_out ? d_ff_5_q : 1'bz;  // Controlled_Buffer controlled_buffer_21
  assign BUS_out[5] = MDR_out ? d_ff_6_q : 1'bz;  // Controlled_Buffer controlled_buffer_22
  assign BUS_out[6] = MDR_out ? d_ff_7_q : 1'bz;  // Controlled_Buffer controlled_buffer_23
  assign BUS_out[7] = MDR_out ? d_ff_8_q : 1'bz;  // Controlled_Buffer controlled_buffer_24
  assign BUS_out[8] = MDR_out ? d_ff_9_q : 1'bz;  // Controlled_Buffer controlled_buffer_25
  assign BUS_out[9] = MDR_out ? d_ff_10_q : 1'bz;  // Controlled_Buffer controlled_buffer_26
  assign BUS_out[10] = MDR_out ? d_ff_11_q : 1'bz;  // Controlled_Buffer controlled_buffer_27
  assign BUS_out[11] = MDR_out ? d_ff_12_q : 1'bz;  // Controlled_Buffer controlled_buffer_28
  assign BUS_out[12] = MDR_out ? d_ff_13_q : 1'bz;  // Controlled_Buffer controlled_buffer_29
  assign BUS_out[13] = MDR_out ? d_ff_14_q : 1'bz;  // Controlled_Buffer controlled_buffer_30
  assign BUS_out[14] = MDR_out ? d_ff_15_q : 1'bz;  // Controlled_Buffer controlled_buffer_31
  assign BUS_out[15] = MDR_out ? d_ff_16_q : 1'bz;  // Controlled_Buffer controlled_buffer_32
endmodule

module PSW (
  input  IR_S,
  input  [15:0] bus_input,
  input  Z_in,
  input  PSW_out,
  input  [3:0] IR_opcode,
  input  PSW_in,
  input  CC_Z_in,
  input  CC_N_in,
  output [15:0] bus_output,
  output CC_Z,
  output CC_N,
  output P
);

  wire and_1_out, controlled_buffer_1_out, controlled_buffer_3_out, d_ff_4_q, d_ff_5_q, d_ff_6_q, d_ff_7_q,
       d_ff_8_q, d_ff_9_q, d_ff_10_q, d_ff_11_q, d_ff_12_q, d_ff_13_q, d_ff_14_q, d_ff_15_q, d_ff_16_q,
       decoder_1_out0, decoder_1_out1, decoder_1_out2, decoder_1_out3, decoder_1_out4, decoder_1_out5,
       not_1_out, not_2_out, or_1_out, or_2_out;

  Decoder #(.enable("false"), .select(4)) decoder_1 (
    .out0(decoder_1_out0), .out1(decoder_1_out1), .out2(decoder_1_out2), .out3(decoder_1_out3),
    .out4(decoder_1_out4), .out5(decoder_1_out5), .sel(IR_opcode));  // open: out6, out7, out8, out9, out10, out11, out12, out13, out14, out15
  or or_1 (or_1_out, decoder_1_out0, decoder_1_out1, decoder_1_out2, decoder_1_out3, decoder_1_out4, decoder_1_out5);
  not not_1 (not_1_out, and_1_out);
  assign controlled_buffer_1_out = not_1_out ? bus_input[0] : 1'bz;  // Controlled_Buffer controlled_buffer_1
  assign controlled_buffer_1_out = and_1_out ? CC_Z_in : 1'bz;  // Controlled_Buffer controlled_buffer_2
  assign controlled_buffer_3_out = not_1_out ? bus_input[1] : 1'bz;  // Controlled_Buffer controlled_buffer_3
  assign controlled_buffer_3_out = and_1_out ? CC_N_in : 1'bz;  // Controlled_Buffer controlled_buffer_4
  and and_1 (and_1_out, or_1_out, IR_S, Z_in, not_2_out);
  not not_2 (not_2_out, PSW_in);
  or or_2 (or_2_out, and_1_out, PSW_in);
  D_Flip_Flop d_ff_1 (.D(controlled_buffer_1_out), .clk(or_2_out), .Q(CC_Z));  // open: Qn, preset, reset
  D_Flip_Flop d_ff_2 (.D(controlled_buffer_3_out), .clk(or_2_out), .Q(CC_N));  // open: Qn, preset, reset
  D_Flip_Flop d_ff_3 (.D(bus_input[2]), .clk(PSW_in), .Q(P));  // open: Qn, preset, reset
  D_Flip_Flop d_ff_4 (.D(bus_input[3]), .clk(PSW_in), .Q(d_ff_4_q));  // open: Qn, preset, reset
  D_Flip_Flop d_ff_5 (.D(bus_input[4]), .clk(PSW_in), .Q(d_ff_5_q));  // open: Qn, preset, reset
  D_Flip_Flop d_ff_6 (.D(bus_input[5]), .clk(PSW_in), .Q(d_ff_6_q));  // open: Qn, preset, reset
  D_Flip_Flop d_ff_7 (.D(bus_input[6]), .clk(PSW_in), .Q(d_ff_7_q));  // open: Qn, preset, reset
  D_Flip_Flop d_ff_8 (.D(bus_input[7]), .clk(PSW_in), .Q(d_ff_8_q));  // open: Qn, preset, reset
  D_Flip_Flop d_ff_9 (.D(bus_input[8]), .clk(PSW_in), .Q(d_ff_9_q));  // open: Qn, preset, reset
  D_Flip_Flop d_ff_10 (.D(bus_input[9]), .clk(PSW_in), .Q(d_ff_10_q));  // open: Qn, preset, reset
  D_Flip_Flop d_ff_11 (.D(bus_input[10]), .clk(PSW_in), .Q(d_ff_11_q));  // open: Qn, preset, reset
  D_Flip_Flop d_ff_12 (.D(bus_input[11]), .clk(PSW_in), .Q(d_ff_12_q));  // open: Qn, preset, reset
  D_Flip_Flop d_ff_13 (.D(bus_input[12]), .clk(PSW_in), .Q(d_ff_13_q));  // open: Qn, preset, reset
  D_Flip_Flop d_ff_14 (.D(bus_input[13]), .clk(PSW_in), .Q(d_ff_14_q));  // open: Qn, preset, reset
  D_Flip_Flop d_ff_15 (.D(bus_input[14]), .clk(PSW_in), .Q(d_ff_15_q));  // open: Qn, preset, reset
  D_Flip_Flop d_ff_16 (.D(bus_input[15]), .clk(PSW_in), .Q(d_ff_16_q));  // open: Qn, preset, reset
  assign bus_output[0] = PSW_out ? CC_Z : 1'bz;  // Controlled_Buffer controlled_buffer_5
  assign bus_output[1] = PSW_out ? CC_N : 1'bz;  // Controlled_Buffer controlled_buffer_6
  assign bus_output[2] = PSW_out ? P : 1'bz;  // Controlled_Buffer controlled_buffer_7
  assign bus_output[3] = PSW_out ? d_ff_4_q : 1'bz;  // Controlled_Buffer controlled_buffer_8
  assign bus_output[4] = PSW_out ? d_ff_5_q : 1'bz;  // Controlled_Buffer controlled_buffer_9
  assign bus_output[5] = PSW_out ? d_ff_6_q : 1'bz;  // Controlled_Buffer controlled_buffer_10
  assign bus_output[6] = PSW_out ? d_ff_7_q : 1'bz;  // Controlled_Buffer controlled_buffer_11
  assign bus_output[7] = PSW_out ? d_ff_8_q : 1'bz;  // Controlled_Buffer controlled_buffer_12
  assign bus_output[8] = PSW_out ? d_ff_9_q : 1'bz;  // Controlled_Buffer controlled_buffer_13
  assign bus_output[9] = PSW_out ? d_ff_10_q : 1'bz;  // Controlled_Buffer controlled_buffer_14
  assign bus_output[10] = PSW_out ? d_ff_11_q : 1'bz;  // Controlled_Buffer controlled_buffer_15
  assign bus_output[11] = PSW_out ? d_ff_12_q : 1'bz;  // Controlled_Buffer controlled_buffer_16
  assign bus_output[12] = PSW_out ? d_ff_13_q : 1'bz;  // Controlled_Buffer controlled_buffer_17
  assign bus_output[13] = PSW_out ? d_ff_14_q : 1'bz;  // Controlled_Buffer controlled_buffer_18
  assign bus_output[14] = PSW_out ? d_ff_15_q : 1'bz;  // Controlled_Buffer controlled_buffer_19
  assign bus_output[15] = PSW_out ? d_ff_16_q : 1'bz;  // Controlled_Buffer controlled_buffer_20
endmodule

module single_shifter (
  input  [15:0] data_input,
  input  right_shift,
  output [15:0] data_out
);

  wire and_1_out, and_2_out, and_3_out, and_4_out, and_5_out, and_6_out, and_7_out, and_8_out, and_9_out,
       and_10_out, and_11_out, and_12_out, and_13_out, and_14_out, and_15_out, and_16_out, and_17_out,
       and_18_out, and_19_out, and_20_out, and_21_out, and_22_out, and_23_out, and_24_out, and_25_out,
       and_26_out, and_27_out, and_28_out, and_29_out, and_30_out, and_32_out, not_1_out;

  not not_1 (not_1_out, right_shift);
  and and_1 (and_1_out, data_input[15], right_shift);
  and and_2 (and_2_out, not_1_out, data_input[14]);
  and and_3 (and_3_out, and_2_out, not_1_out);
  and and_4 (and_4_out, data_input[14], right_shift);
  and and_5 (and_5_out, not_1_out, data_input[13]);
  or or_1 (data_out[14], and_1_out, and_5_out);
  and and_6 (and_6_out, data_out[14], right_shift);
  and and_7 (and_7_out, data_input[13], right_shift);
  or or_2 (data_out[13], and_4_out, and_8_out);
  or or_3 (data_out[15], and_6_out, and_3_out);
  and and_8 (and_8_out, not_1_out, data_input[12]);
  and and_9 (and_9_out, data_input[12], right_shift);
  or or_4 (data_out[12], and_7_out, and_10_out);
  and and_10 (and_10_out, not_1_out, data_input[11]);
  and and_11 (and_11_out, data_input[11], right_shift);
  or or_5 (data_out[11], and_9_out, and_12_out);
  and and_12 (and_12_out, not_1_out, data_input[10]);
  and and_13 (and_13_out, data_input[10], right_shift);
  or or_6 (data_out[10], and_11_out, and_14_out);
  and and_14 (and_14_out, not_1_out, data_input[9]);
  and and_15 (and_15_out, data_input[9], right_shift);
  or or_7 (data_out[9], and_13_out, and_16_out);
  and and_16 (and_16_out, right_shift, data_input[8]);
  or or_8 (data_out[8], and_15_out, and_17_out);
  and and_17 (and_17_out, not_1_out, data_input[7]);
  and and_18 (and_18_out, data_input[8], right_shift);
  or or_9 (data_out[7], and_18_out, and_20_out);
  and and_19 (and_19_out, data_input[7], right_shift);
  and and_20 (and_20_out, not_1_out, data_input[6]);
  and and_21 (and_21_out, data_input[6], right_shift);
  and and_22 (and_22_out, not_1_out, data_input[5]);
  or or_10 (data_out[6], and_19_out, and_22_out);
  and and_23 (and_23_out, data_input[5], right_shift);
  or or_11 (data_out[5], and_21_out, and_24_out);
  and and_24 (and_24_out, not_1_out, data_input[4]);
  and and_25 (and_25_out, data_input[4], right_shift);
  or or_12 (data_out[4], and_23_out, and_26_out);
  and and_26 (and_26_out, not_1_out, data_input[3]);
  and and_27 (and_27_out, data_input[3], right_shift);
  or or_13 (data_out[3], and_25_out, and_28_out);
  and and_28 (and_28_out, not_1_out, data_input[2]);
  and and_29 (and_29_out, data_input[2], right_shift);
  or or_14 (data_out[2], and_27_out, and_30_out);
  and and_30 (and_30_out, not_1_out, data_input[1]);
  and and_31 (data_out[0], data_input[1], right_shift);
  or or_15 (data_out[1], and_29_out, and_32_out);
  and and_32 (and_32_out, not_1_out, data_input[0]);
endmodule

module Shift (
  input  Y_shift_right,
  input  [15:0] from_Y,
  input  Y_shift_left,
  input  [1:0] shift_amount,
  output [15:0] to_ALU
);

  wire nor_1_out, not_1_out, not_2_out;
  wire [15:0] multiplexer_1_out, single_shifter_1_data_out, single_shifter_2_data_out,
       single_shifter_3_data_out;

  not not_1 (not_1_out, Y_shift_left);
  single_shifter single_shifter_1 (.data_input(from_Y), .right_shift(not_1_out), .data_out(single_shifter_1_data_out));
  single_shifter single_shifter_2 (
    .data_input(single_shifter_1_data_out), .right_shift(not_1_out), .data_out(single_shifter_2_data_out));
  single_shifter single_shifter_3 (
    .data_input(single_shifter_2_data_out), .right_shift(not_1_out), .data_out(single_shifter_3_data_out));
  nor nor_1 (nor_1_out, Y_shift_right, Y_shift_left);
  assign to_ALU = nor_1_out ? from_Y : 16'bz;  // Controlled_Buffer controlled_buffer_1
  not not_2 (not_2_out, nor_1_out);
  Multiplexer #(.select(2), .width(16)) multiplexer_1 (
    .in0(from_Y), .in1(single_shifter_1_data_out), .in2(single_shifter_2_data_out),
    .in3(single_shifter_3_data_out), .out(multiplexer_1_out), .sel(shift_amount));
  assign to_ALU = not_2_out ? multiplexer_1_out : 16'bz;  // Controlled_Buffer controlled_buffer_2
endmodule

module CONROM (
  input  ROM_8_Out,
  output [15:0] Bus_output
);

  assign Bus_output = ROM_8_Out ? 16'h8 : 16'bz;  // Controlled_Buffer controlled_buffer_1
endmodule

module timer (
  input  Timer_In,
  input  Clock,
  input  [15:0] Bus_input,
  output TIMEOUT
);

  Counter #(.max('hffff), .ongoal("stay"), .width(16)) counter_1 (
    .load(Timer_In), .up(1'b0), .clk(Clock), .D(Bus_input), .carry(TIMEOUT));  // open: clr, count, Q
endmodule

module Y (
  input  Y_in,
  input  Y_offset_in,
  input  [15:0] BUS_in,
  input  Y_out,
  output [15:0] To_shifter,
  output [15:0] Bus_output
);

  wire and_1_out, and_2_out, and_3_out, and_4_out, and_5_out, and_6_out, and_7_out, and_8_out, and_9_out,
       and_10_out, and_11_out, and_12_out, and_13_out, and_14_out, and_15_out, and_16_out, and_17_out,
       and_18_out, and_19_out, and_20_out, and_21_out, and_22_out, and_23_out, and_24_out, and_25_out,
       and_26_out, and_27_out, and_28_out, and_29_out, and_30_out, and_31_out, and_32_out, or_1_out,
       or_2_out, or_3_out, or_4_out, or_5_out, or_6_out, or_7_out, or_8_out, or_9_out, or_10_out, or_11_out,
       or_12_out, or_13_out, or_14_out, or_15_out, or_16_out, xor_1_out;
  wire [15:0] bus_to_offset_sign_extended_1_bus_out;

  Bus_to_offset_sign_extended bus_to_offset_sign_extended_1 (
    .BUS_in(BUS_in), .BUS_out(bus_to_offset_sign_extended_1_bus_out));
  and and_1 (and_1_out, BUS_in[0], Y_in);
  and and_2 (and_2_out, BUS_in[1], Y_in);
  and and_3 (and_3_out, BUS_in[2], Y_in);
  and and_4 (and_4_out, BUS_in[3], Y_in);
  and and_5 (and_5_out, BUS_in[4], Y_in);
  and and_6 (and_6_out, BUS_in[5], Y_in);
  and and_7 (and_7_out, BUS_in[6], Y_in);
  and and_8 (and_8_out, BUS_in[7], Y_in);
  and and_9 (and_9_out, BUS_in[8], Y_in);
  and and_10 (and_10_out, BUS_in[9], Y_in);
  and and_11 (and_11_out, BUS_in[10], Y_in);
  and and_12 (and_12_out, BUS_in[11], Y_in);
  and and_13 (and_13_out, BUS_in[12], Y_in);
  and and_14 (and_14_out, BUS_in[13], Y_in);
  and and_15 (and_15_out, BUS_in[14], Y_in);
  and and_16 (and_16_out, BUS_in[15], Y_in);
  xor xor_1 (xor_1_out, Y_in, Y_offset_in);
  and and_17 (and_17_out, Y_offset_in, bus_to_offset_sign_extended_1_bus_out[0]);
  or or_1 (or_1_out, and_17_out, and_1_out);
  and and_18 (and_18_out, Y_offset_in, bus_to_offset_sign_extended_1_bus_out[1]);
  or or_2 (or_2_out, and_18_out, and_2_out);
  and and_19 (and_19_out, Y_offset_in, bus_to_offset_sign_extended_1_bus_out[2]);
  or or_3 (or_3_out, and_19_out, and_3_out);
  and and_20 (and_20_out, Y_offset_in, bus_to_offset_sign_extended_1_bus_out[3]);
  or or_4 (or_4_out, and_20_out, and_4_out);
  and and_21 (and_21_out, Y_offset_in, bus_to_offset_sign_extended_1_bus_out[4]);
  or or_5 (or_5_out, and_21_out, and_5_out);
  and and_22 (and_22_out, Y_offset_in, bus_to_offset_sign_extended_1_bus_out[5]);
  or or_6 (or_6_out, and_22_out, and_6_out);
  and and_23 (and_23_out, Y_offset_in, bus_to_offset_sign_extended_1_bus_out[6]);
  or or_7 (or_7_out, and_23_out, and_7_out);
  and and_24 (and_24_out, Y_offset_in, bus_to_offset_sign_extended_1_bus_out[7]);
  or or_8 (or_8_out, and_24_out, and_8_out);
  and and_25 (and_25_out, Y_offset_in, bus_to_offset_sign_extended_1_bus_out[8]);
  or or_9 (or_9_out, and_25_out, and_9_out);
  and and_26 (and_26_out, Y_offset_in, bus_to_offset_sign_extended_1_bus_out[9]);
  or or_10 (or_10_out, and_26_out, and_10_out);
  and and_27 (and_27_out, Y_offset_in, bus_to_offset_sign_extended_1_bus_out[10]);
  or or_11 (or_11_out, and_27_out, and_11_out);
  and and_28 (and_28_out, Y_offset_in, bus_to_offset_sign_extended_1_bus_out[11]);
  or or_12 (or_12_out, and_28_out, and_12_out);
  and and_29 (and_29_out, Y_offset_in, bus_to_offset_sign_extended_1_bus_out[12]);
  or or_13 (or_13_out, and_29_out, and_13_out);
  and and_30 (and_30_out, Y_offset_in, bus_to_offset_sign_extended_1_bus_out[13]);
  or or_14 (or_14_out, and_30_out, and_14_out);
  and and_31 (and_31_out, Y_offset_in, bus_to_offset_sign_extended_1_bus_out[14]);
  or or_15 (or_15_out, and_31_out, and_15_out);
  and and_32 (and_32_out, Y_offset_in, bus_to_offset_sign_extended_1_bus_out[15]);
  or or_16 (or_16_out, and_32_out, and_16_out);
  D_Flip_Flop d_ff_1 (.D(or_1_out), .clk(xor_1_out), .Q(To_shifter[0]));  // open: Qn, preset, reset
  D_Flip_Flop d_ff_2 (.D(or_2_out), .clk(xor_1_out), .Q(To_shifter[1]));  // open: Qn, preset, reset
  D_Flip_Flop d_ff_3 (.D(or_3_out), .clk(xor_1_out), .Q(To_shifter[2]));  // open: Qn, preset, reset
  D_Flip_Flop d_ff_4 (.D(or_4_out), .clk(xor_1_out), .Q(To_shifter[3]));  // open: Qn, preset, reset
  D_Flip_Flop d_ff_5 (.D(or_5_out), .clk(xor_1_out), .Q(To_shifter[4]));  // open: Qn, preset, reset
  D_Flip_Flop d_ff_6 (.D(or_6_out), .clk(xor_1_out), .Q(To_shifter[5]));  // open: Qn, preset, reset
  D_Flip_Flop d_ff_7 (.D(or_7_out), .clk(xor_1_out), .Q(To_shifter[6]));  // open: Qn, preset, reset
  D_Flip_Flop d_ff_8 (.D(or_8_out), .clk(xor_1_out), .Q(To_shifter[7]));  // open: Qn, preset, reset
  D_Flip_Flop d_ff_9 (.D(or_9_out), .clk(xor_1_out), .Q(To_shifter[8]));  // open: Qn, preset, reset
  D_Flip_Flop d_ff_10 (.D(or_10_out), .clk(xor_1_out), .Q(To_shifter[9]));  // open: Qn, preset, reset
  D_Flip_Flop d_ff_11 (.D(or_11_out), .clk(xor_1_out), .Q(To_shifter[10]));  // open: Qn, preset, reset
  D_Flip_Flop d_ff_12 (.D(or_12_out), .clk(xor_1_out), .Q(To_shifter[11]));  // open: Qn, preset, reset
  D_Flip_Flop d_ff_13 (.D(or_13_out), .clk(xor_1_out), .Q(To_shifter[12]));  // open: Qn, preset, reset
  D_Flip_Flop d_ff_14 (.D(or_14_out), .clk(xor_1_out), .Q(To_shifter[13]));  // open: Qn, preset, reset
  D_Flip_Flop d_ff_15 (.D(or_15_out), .clk(xor_1_out), .Q(To_shifter[14]));  // open: Qn, preset, reset
  D_Flip_Flop d_ff_16 (.D(or_16_out), .clk(xor_1_out), .Q(To_shifter[15]));  // open: Qn, preset, reset
  assign Bus_output[0] = Y_out ? To_shifter[0] : 1'bz;  // Controlled_Buffer controlled_buffer_1
  assign Bus_output[1] = Y_out ? To_shifter[1] : 1'bz;  // Controlled_Buffer controlled_buffer_2
  assign Bus_output[2] = Y_out ? To_shifter[2] : 1'bz;  // Controlled_Buffer controlled_buffer_3
  assign Bus_output[3] = Y_out ? To_shifter[3] : 1'bz;  // Controlled_Buffer controlled_buffer_4
  assign Bus_output[4] = Y_out ? To_shifter[4] : 1'bz;  // Controlled_Buffer controlled_buffer_5
  assign Bus_output[5] = Y_out ? To_shifter[5] : 1'bz;  // Controlled_Buffer controlled_buffer_6
  assign Bus_output[6] = Y_out ? To_shifter[6] : 1'bz;  // Controlled_Buffer controlled_buffer_7
  assign Bus_output[7] = Y_out ? To_shifter[7] : 1'bz;  // Controlled_Buffer controlled_buffer_8
  assign Bus_output[8] = Y_out ? To_shifter[8] : 1'bz;  // Controlled_Buffer controlled_buffer_9
  assign Bus_output[9] = Y_out ? To_shifter[9] : 1'bz;  // Controlled_Buffer controlled_buffer_10
  assign Bus_output[10] = Y_out ? To_shifter[10] : 1'bz;  // Controlled_Buffer controlled_buffer_11
  assign Bus_output[11] = Y_out ? To_shifter[11] : 1'bz;  // Controlled_Buffer controlled_buffer_12
  assign Bus_output[12] = Y_out ? To_shifter[12] : 1'bz;  // Controlled_Buffer controlled_buffer_13
  assign Bus_output[13] = Y_out ? To_shifter[13] : 1'bz;  // Controlled_Buffer controlled_buffer_14
  assign Bus_output[14] = Y_out ? To_shifter[14] : 1'bz;  // Controlled_Buffer controlled_buffer_15
  assign Bus_output[15] = Y_out ? To_shifter[15] : 1'bz;  // Controlled_Buffer controlled_buffer_16
endmodule

module Bus_to_offset_sign_extended (
  input  [15:0] BUS_in,
  output [15:0] BUS_out
);


  assign BUS_out = {BUS_in[15:7], {7{BUS_in[7]}}};
endmodule

module Z (
  input  Zin,
  input  [15:0] ALU_input,
  input  Zout,
  output [15:0] BUS_out
);

  wire ms_1_sout, ms_2_sout, ms_3_sout, ms_4_sout, ms_5_sout, ms_6_sout, ms_7_sout, ms_8_sout, ms_9_sout,
       ms_10_sout, ms_11_sout, ms_12_sout, ms_13_sout, ms_14_sout, ms_15_sout, ms_16_sout;

  MS ms_1 (.MSbit(ALU_input[0]), .Enable(Zin), .Sout(ms_1_sout));
  MS ms_2 (.MSbit(ALU_input[1]), .Enable(Zin), .Sout(ms_2_sout));
  MS ms_3 (.MSbit(ALU_input[2]), .Enable(Zin), .Sout(ms_3_sout));
  MS ms_4 (.MSbit(ALU_input[3]), .Enable(Zin), .Sout(ms_4_sout));
  MS ms_5 (.MSbit(ALU_input[4]), .Enable(Zin), .Sout(ms_5_sout));
  MS ms_6 (.MSbit(ALU_input[5]), .Enable(Zin), .Sout(ms_6_sout));
  MS ms_7 (.MSbit(ALU_input[6]), .Enable(Zin), .Sout(ms_7_sout));
  MS ms_8 (.MSbit(ALU_input[7]), .Enable(Zin), .Sout(ms_8_sout));
  MS ms_9 (.MSbit(ALU_input[8]), .Enable(Zin), .Sout(ms_9_sout));
  MS ms_10 (.MSbit(ALU_input[9]), .Enable(Zin), .Sout(ms_10_sout));
  MS ms_11 (.MSbit(ALU_input[10]), .Enable(Zin), .Sout(ms_11_sout));
  MS ms_12 (.MSbit(ALU_input[11]), .Enable(Zin), .Sout(ms_12_sout));
  MS ms_13 (.MSbit(ALU_input[12]), .Enable(Zin), .Sout(ms_13_sout));
  MS ms_14 (.MSbit(ALU_input[13]), .Enable(Zin), .Sout(ms_14_sout));
  MS ms_15 (.MSbit(ALU_input[14]), .Enable(Zin), .Sout(ms_15_sout));
  MS ms_16 (.MSbit(ALU_input[15]), .Enable(Zin), .Sout(ms_16_sout));
  assign BUS_out[0] = Zout ? ms_1_sout : 1'bz;  // Controlled_Buffer controlled_buffer_1
  assign BUS_out[1] = Zout ? ms_2_sout : 1'bz;  // Controlled_Buffer controlled_buffer_2
  assign BUS_out[2] = Zout ? ms_3_sout : 1'bz;  // Controlled_Buffer controlled_buffer_3
  assign BUS_out[3] = Zout ? ms_4_sout : 1'bz;  // Controlled_Buffer controlled_buffer_4
  assign BUS_out[4] = Zout ? ms_5_sout : 1'bz;  // Controlled_Buffer controlled_buffer_5
  assign BUS_out[5] = Zout ? ms_6_sout : 1'bz;  // Controlled_Buffer controlled_buffer_6
  assign BUS_out[6] = Zout ? ms_7_sout : 1'bz;  // Controlled_Buffer controlled_buffer_7
  assign BUS_out[7] = Zout ? ms_8_sout : 1'bz;  // Controlled_Buffer controlled_buffer_8
  assign BUS_out[8] = Zout ? ms_9_sout : 1'bz;  // Controlled_Buffer controlled_buffer_9
  assign BUS_out[9] = Zout ? ms_10_sout : 1'bz;  // Controlled_Buffer controlled_buffer_10
  assign BUS_out[10] = Zout ? ms_11_sout : 1'bz;  // Controlled_Buffer controlled_buffer_11
  assign BUS_out[11] = Zout ? ms_12_sout : 1'bz;  // Controlled_Buffer controlled_buffer_12
  assign BUS_out[12] = Zout ? ms_13_sout : 1'bz;  // Controlled_Buffer controlled_buffer_13
  assign BUS_out[13] = Zout ? ms_14_sout : 1'bz;  // Controlled_Buffer controlled_buffer_14
  assign BUS_out[14] = Zout ? ms_15_sout : 1'bz;  // Controlled_Buffer controlled_buffer_15
  assign BUS_out[15] = Zout ? ms_16_sout : 1'bz;  // Controlled_Buffer controlled_buffer_16
endmodule

module MS (
  input  MSbit,
  input  Enable,
  output Sout
);

  wire d_ff_1_q, not_1_out;

  D_Flip_Flop d_ff_1 (.D(MSbit), .clk(Enable), .Q(d_ff_1_q));  // open: Qn, preset, reset
  D_Flip_Flop d_ff_2 (.D(d_ff_1_q), .clk(not_1_out), .Q(Sout));  // open: Qn, preset, reset
  not not_1 (not_1_out, Enable);
endmodule

module RA_M (
  input  [15:0] MAR_To_MM,
  input  Load_MM,
  input  Read_MM,
  input  [15:0] MDR_To_MM,
  output [15:0] MDR_From_MM
);

  wire or_1_out;

  RAM #(.addrWidth(16), .dataWidth(16)) ram_1 (
    .addr(MAR_To_MM), .we(Load_MM), .oe(Read_MM), .clk(or_1_out), .din(MDR_To_MM), .dout(MDR_From_MM));
  or or_1 (or_1_out, Read_MM, Load_MM);
endmodule

module main_testing (
);

  wire comp_arator_1_cc_z, control_unit_1_clck, control_unit_1_gpr_in, control_unit_1_gpr_out,
       control_unit_1_ir_in, control_unit_1_load_mm, control_unit_1_mar_in, control_unit_1_mdr_in,
       control_unit_1_mdr_out, control_unit_1_psw_in, control_unit_1_psw_out, control_unit_1_read_mm,
       control_unit_1_rom_8_out, control_unit_1_timer_in, control_unit_1_y_in, control_unit_1_y_offset_in,
       control_unit_1_y_out, control_unit_1_y_shift_left, control_unit_1_y_shift_right, control_unit_1_z_in,
       control_unit_1_z_out, ir_1_s, timer_1_timeout;
  wire [1:0] ir_1_shift;
  wire [2:0] control_unit_1_alu_control, control_unit_1_gpr_select, ir_1_rd_out_1, ir_1_rd_out_2, ir_1_rs1,
       ir_1_rs2, psw_1_cc_z;
  wire [3:0] ir_1_opcode_out;
  wire [15:0] alu_1_alu_out, mar_1_to_mm, mdr_new_1_bus_out, mdr_new_1_to_mm, ra_m_1_mdr_from_mm,
       shift_1_to_alu, y_1_to_shifter;

  MAR mar_1 (
    .BUS_in(mdr_new_1_bus_out), .MAR_in(control_unit_1_mar_in), .Read_MM(control_unit_1_read_mm),
    .Load_MM(control_unit_1_load_mm), .To_MM(mar_1_to_mm));
  RA_M ra_m_1 (
    .MAR_To_MM(mar_1_to_mm), .Load_MM(control_unit_1_load_mm), .Read_MM(control_unit_1_read_mm),
    .MDR_To_MM(mdr_new_1_to_mm), .MDR_From_MM(ra_m_1_mdr_from_mm));
  MDR_new mdr_new_1 (
    .MDR_in(control_unit_1_mdr_in), .Read_MM(control_unit_1_read_mm), .BUS_in(mdr_new_1_bus_out),
    .MDR_out(control_unit_1_mdr_out), .Load_MM(control_unit_1_load_mm), .From_MM(ra_m_1_mdr_from_mm),
    .BUS_out(mdr_new_1_bus_out), .To_MM(mdr_new_1_to_mm));
  IR ir_1 (
    .BUS_in(mdr_new_1_bus_out), .IR_in(control_unit_1_ir_in), .Rd_out_2(ir_1_rd_out_2), .Rs1(ir_1_rs1),
    .Rs2(ir_1_rs2), .Rd_out_1(ir_1_rd_out_1), .OPCODE_out(ir_1_opcode_out), .S(ir_1_s), .Shift(ir_1_shift));
  control_unit control_unit_1 (
    .IR_opcode(ir_1_opcode_out), .PSW_0_1_2(psw_1_cc_z), .IR_Rs2(ir_1_rs2), .TIMEOUT(timer_1_timeout),
    .ALU_control(control_unit_1_alu_control), .Clck(control_unit_1_clck), .GPR_in(control_unit_1_gpr_in),
    .GPR_out(control_unit_1_gpr_out), .GPR_select(control_unit_1_gpr_select), .IR_in(control_unit_1_ir_in),
    .Load_MM(control_unit_1_load_mm), .MAR_in(control_unit_1_mar_in), .MDR_in(control_unit_1_mdr_in),
    .MDR_out(control_unit_1_mdr_out), .PSW_in(control_unit_1_psw_in), .PSW_out(control_unit_1_psw_out),
    .Read_MM(control_unit_1_read_mm), .ROM_8_out(control_unit_1_rom_8_out),
    .Timer_In(control_unit_1_timer_in), .Y_in(control_unit_1_y_in), .Y_offset_in(control_unit_1_y_offset_in),
    .Y_out(control_unit_1_y_out), .Y_shift_left(control_unit_1_y_shift_left),
    .Y_shift_right(control_unit_1_y_shift_right), .Z_in(control_unit_1_z_in), .Z_out(control_unit_1_z_out));
  GPR_Full gpr_full_1 (
    .Rd_1(ir_1_rd_out_1), .Rd_2(ir_1_rd_out_2), .Rs_1(ir_1_rs1), .Rs_2(ir_1_rs2),
    .GPR_in(control_unit_1_gpr_in), .GPR_out(control_unit_1_gpr_out), .BUS_in(mdr_new_1_bus_out),
    .GPR_sel(control_unit_1_gpr_select), .BUS_out(mdr_new_1_bus_out));
  Y y_1 (
    .Y_in(control_unit_1_y_in), .Y_offset_in(control_unit_1_y_offset_in), .BUS_in(mdr_new_1_bus_out),
    .Y_out(control_unit_1_y_out), .To_shifter(y_1_to_shifter), .Bus_output(mdr_new_1_bus_out));
  Shift shift_1 (
    .Y_shift_right(control_unit_1_y_shift_right), .from_Y(y_1_to_shifter),
    .Y_shift_left(control_unit_1_y_shift_left), .shift_amount(ir_1_shift), .to_ALU(shift_1_to_alu));
  timer timer_1 (
    .Timer_In(control_unit_1_timer_in), .Clock(control_unit_1_clck), .Bus_input(mdr_new_1_bus_out),
    .TIMEOUT(timer_1_timeout));
  ALU alu_1 (
    .ALU_control(control_unit_1_alu_control), .bus_input(mdr_new_1_bus_out),
    .Y_shifted_input(shift_1_to_alu), .ALU_out(alu_1_alu_out));
  CONROM conrom_1 (.ROM_8_Out(control_unit_1_rom_8_out), .Bus_output(mdr_new_1_bus_out));
  Z z_1 (
    .Zin(control_unit_1_z_in), .ALU_input(alu_1_alu_out), .Zout(control_unit_1_z_out),
    .BUS_out(mdr_new_1_bus_out));
  Comp_arator comp_arator_1 (.from_ALU(alu_1_alu_out), .CC_Z(comp_arator_1_cc_z), .CC_N(comp_arator_1_cc_z));
  PSW psw_1 (
    .IR_S(ir_1_s), .bus_input(mdr_new_1_bus_out), .Z_in(control_unit_1_z_in),
    .PSW_out(control_unit_1_psw_out), .IR_opcode(ir_1_opcode_out), .PSW_in(control_unit_1_psw_in),
    .CC_Z_in(comp_arator_1_cc_z), .CC_N_in(comp_arator_1_cc_z), .bus_output(mdr_new_1_bus_out),
    .CC_Z(psw_1_cc_z[0]), .CC_N(psw_1_cc_z[1]), .P(psw_1_cc_z[2]));
endmodule
